// Logisim project Vrata_Version0.0.2.circ as structural Verilog: 7 circuits, main circuit main
module main (
);

  wire button_1_out, \functionality_1_otevírání , \functionality_1_otevřeno , \functionality_1_zavíraní ,
       \functionality_1_zavřeno ;
  wire [3:0] functionality_1_leva, functionality_1_prava;
  wire [31:0] dotmatrix_1_p1, dotmatrix_1_p2, matrixvrata_1_prava_cast;

  Button button_1 (.out(button_1_out));
  LED led_1 (.in(\functionality_1_otevírání ));
  LED led_2 (.in(\functionality_1_otevřeno ));
  LED led_3 (.in(\functionality_1_zavíraní ));
  LED led_4 (.in(\functionality_1_zavřeno ));
  functionality functionality_1 (
    .Button(button_1_out), .\Otevírání (\functionality_1_otevírání ),
    .\Otevřeno (\functionality_1_otevřeno ), .\Zavíraní (\functionality_1_zavíraní ),
    .\Zavřeno (\functionality_1_zavřeno ), .Leva(functionality_1_leva), .Prava(functionality_1_prava));
  // DotMatrix #(.inputtype("select"), .matrixcols(32), .matrixrows(32)) dotmatrix_1: pin names not known; wires that end beside it: dotmatrix_1_p1, dotmatrix_1_p2
  MatrixVrata matrixvrata_1 (
    .LEVA_CAST(dotmatrix_1_p1), .PRAVA_CAST(matrixvrata_1_prava_cast), .Leve_Dvere(functionality_1_leva),
    .Prave_dvere(functionality_1_prava), .Vyska_dveri(dotmatrix_1_p2));
  // DotMatrix #(.inputtype("select"), .matrixrows(32)) dotmatrix_2: pin names not known; wires that end beside it: {5{1'b1}}, {32{1'b1}}
  // DotMatrix #(.inputtype("select"), .matrixcols(32), .matrixrows(32)) dotmatrix_3: pin names not known; wires that end beside it: matrixvrata_1_prava_cast, dotmatrix_1_p2

  // Notes on the sheet:
  //   START/STOP
  //   Bug jestli se automaticky dveře zavírají, tak při stisku tlačítka se nezačnou otevírat
endmodule

module buttonswitch (
  input  Reset,
  input  Button,
  output \Output___Otevřeno_Zavřeno 
);

  wire d_ff_1_qn, d_ff_2_q, or_1_out;

  or or_1 (or_1_out, Button, Reset);
  D_Flip_Flop #(.trigger("high")) d_ff_1 (
    .clk(or_1_out), .D(d_ff_2_q), .Q(\Output___Otevřeno_Zavřeno ), .Qn(d_ff_1_qn));  // open: preset, en, reset
  D_Flip_Flop d_ff_2 (.clk(or_1_out), .D(d_ff_1_qn), .Q(d_ff_2_q));  // open: Qn, preset, en, reset
endmodule

module reset (
  input  Leva_Zavirani,
  input  Leva_Zavreno,
  input  Zavrit,
  input  CLOCK,
  output OUTPUT___RESET
);

  wire and_1_out;

  and and_1 (and_1_out, Leva_Zavirani, Leva_Zavreno, Zavrit);
  Counter #(.width(1), .max('h1), .trigger("falling")) counter_1 (
    .count(and_1_out), .carry(OUTPUT___RESET), .clk(CLOCK), .clr(OUTPUT___RESET));  // open: load, D, Q
endmodule

module functionality (
  input  Button,
  output [3:0] Leva,
  output [3:0] Prava,
  output \Otevírání ,
  output \Otevřeno ,
  output \Zavíraní ,
  output \Zavřeno 
);

  wire and_1_out, and_2_out, and_3_out, and_4_out, AR, AUTO_RESET, BR, clock_1_out, counter_3_carry, CR,
       dotmatrix_1_p1, LO, or_1_out, or_2_out, PO, VZ, ZT;

  Button button_1 ();  // open: out
  Clock #(.highDuration(2), .lowDuration(2)) clock_1 (.out(clock_1_out));
  or or_1 (or_1_out, AUTO_RESET, BR);
  buttonswitch buttonswitch_1 (.Reset(Button), .\Output___Otevřeno_Zavřeno (VZ), .Button(or_1_out));
  display display_1 (
    .\Pravá_Otevřeno (PO), .\Levá_otevřeno (LO), .\Zavřít (ZT), .Zapnuto_Vypnuto(VZ),
    .\Otevírání (\Otevírání ), .\Otevřeno (\Otevřeno ), .\Zavírání (\Zavíraní ), .\Zavřeno (\Zavřeno ));
  zavritdriv zavritdriv_1 (
    .Hodnota_otevreni_zleva(Leva), .On_Off(VZ), .Zavrit_driv(AR), .Button_reset(BR), .Casovac_reset(CR),
    .Auto_Reset(AUTO_RESET));
  and and_1 (and_1_out, ZT, PO);
  and and_2 (and_2_out, VZ, clock_1_out);
  Counter #(.width(4), .max('hf), .ongoal("stay"), .trigger("falling")) counter_1 (
    .load(and_1_out), .Q(Leva), .carry(LO), .clk(and_2_out));  // open: D, count, clr
  reset reset_1 (
    .Leva_Zavirani(LO), .Leva_Zavreno(and_1_out), .Zavrit(ZT), .OUTPUT___RESET(AUTO_RESET),
    .CLOCK(clock_1_out));
  and and_3 (and_3_out, LO, VZ, clock_1_out);
  Counter #(.width(4), .max('hf), .ongoal("stay"), .trigger("falling")) counter_2 (
    .load(ZT), .Q(Prava), .carry(PO), .clk(and_3_out));  // open: D, count, clr
  and and_4 (and_4_out, PO, VZ, clock_1_out);
  // DotMatrix #(.inputtype("select"), .matrixcols(15), .matrixrows(10)) dotmatrix_1: pin names not known; wires that end beside it: dotmatrix_1_p1, dotmatrix_1_p1
  Counter #(.width(3), .max('h7), .ongoal("stay")) counter_3 (
    .carry(counter_3_carry), .clk(and_4_out), .clr(or_2_out));  // open: load, D, count, Q
  or or_2 (or_2_out, CR, AUTO_RESET);
  or or_3 (ZT, counter_3_carry, AR);

  // Other names for the same wires on the sheet: LH[3:0] = Leva; PH[3:0] = Prava
endmodule

module display (
  input  \Pravá_Otevřeno ,
  input  \Levá_otevřeno ,
  input  \Zavřít ,
  input  Zapnuto_Vypnuto,
  output \Otevírání ,
  output \Otevřeno ,
  output \Zavírání ,
  output \Zavřeno 
);

  wire and_3_out, and_4_out, not_2_out, not_3_out, not_4_out, not_5_out, not_6_out;

  not not_1 (\Zavřeno , Zapnuto_Vypnuto);
  not not_2 (not_2_out, \Zavřít );
  not not_3 (not_3_out, \Pravá_Otevřeno );
  not not_4 (not_4_out, \Zavřít );
  not not_5 (not_5_out, \Pravá_Otevřeno );
  not not_6 (not_6_out, \Levá_otevřeno );
  and and_1 (\Otevírání , Zapnuto_Vypnuto, not_2_out, not_3_out);
  and and_2 (\Otevřeno , \Pravá_Otevřeno , not_4_out);
  and and_3 (and_3_out, not_5_out, \Zavřít );
  or or_1 (\Zavírání , and_3_out, and_4_out);
  and and_4 (and_4_out, not_6_out, \Zavřít );
endmodule

module zavritdriv (
  input  [3:0] Hodnota_otevreni_zleva,
  input  On_Off,
  input  Auto_Reset,
  output Zavrit_driv,
  output Button_reset,
  output Casovac_reset
);

  wire and_1_out, comparator_1_eq, comparator_1_gt, counter_1_carry, or_1_out;

  or or_1 (or_1_out, and_1_out, Button_reset, Auto_Reset);
  and and_1 (and_1_out, ~On_Off, counter_1_carry);  // AND_Gate
  Comparator #(.width(4), .mode("unsigned")) comparator_1 (
    .a(Hodnota_otevreni_zleva), .b(4'b0000), .gt(comparator_1_gt), .eq(comparator_1_eq));  // open: lt
  Counter #(.width(2), .max('h2), .ongoal("stay")) counter_1 (
    .carry(counter_1_carry), .clk(On_Off), .clr(or_1_out));  // open: load, D, count, Q
  and and_2 (Zavrit_driv, comparator_1_gt, counter_1_carry);
  and and_3 (Button_reset, comparator_1_eq, counter_1_carry);
  or or_2 (Casovac_reset, Button_reset, and_1_out);
endmodule

module MatrixVrata (
  input  [3:0] Leve_Dvere,
  input  [3:0] Prave_dvere,
  output [31:0] Vyska_dveri,
  output [31:0] LEVA_CAST,
  output [31:0] PRAVA_CAST
);

  wire [2:0] undriven, undriven_2;
  wire [3:0] adder_1_out;
  wire [14:0] multiplexer_3_out;

  Adder #(.width(4)) adder_1 (.a({1'b0, undriven_2}), .b({1'b0, undriven}), .out(adder_1_out));  // open: cin, cout
  Multiplexer #(.select(4), .width(32)) multiplexer_1 (
    .in0({32{1'b1}}), .in1(32'hfffffff), .in2(32'h3ffffff), .in3(32'hffffff), .in4(32'h3fffff),
    .in5(32'hfffff), .in6(32'h3ffff), .in7(32'hffff), .in8(32'h3fff), .in9(32'hfff), .in10(32'h3ff),
    .in11(32'hff), .in12(32'h3f), .in13(32'hf), .in14(32'h3), .in15({32{1'b0}}), .out(LEVA_CAST),
    .sel(Leve_Dvere));  // open: en
  Multiplexer #(.select(4), .width(32)) multiplexer_2 (
    .in0({32{1'b1}}), .in1(32'hfffffff0), .in2(32'hffffffc0), .in3(32'hffffff00), .in4(32'hfffffc00),
    .in5(32'hfffff000), .in6(32'hffffc000), .in7(32'hffff0000), .in8(32'hfffc0000), .in9(32'hfff00000),
    .in10(32'hffc00000), .in11(32'hff000000), .in12(32'hfc000000), .in13(32'hf0000000), .in14(32'hc0000000),
    .in15({32{1'b0}}), .out(PRAVA_CAST), .sel(Prave_dvere));  // open: en
  Multiplexer #(.select(4), .width(15)) multiplexer_3 (
    .in0(15'h7f7f), .in1(15'h7e7f), .in2(15'h7c7f), .in3(15'h787f), .in4(15'h707f), .in5(15'h607f),
    .in6(15'h407f), .in7(15'h7f), .in8(15'h3f), .in9(15'h1f), .in10(15'hf), .in11(15'h7), .in12(15'h3),
    .in13(15'h1), .in14({15{1'b0}}), .in15(15'h707f), .out(multiplexer_3_out), .sel(adder_1_out));  // open: en

  assign Vyska_dveri = 32'hfffffff;
endmodule
