// Logisim project Vrata_Version0.0.5.circ as structural Verilog: 8 circuits, main circuit main
module main (
);

  wire button_2_out, functionality_1_led, \functionality_1_otevírání , \functionality_1_otevřeno ,
       \functionality_1_zavíraní , \functionality_1_zavřeno ;
  wire [3:0] functionality_1_desitky, functionality_1_jednotky, functionality_1_leva, functionality_1_prava;
  wire [31:0] dotmatrix_2_p2, dotmatrix_2_p3, matrixvrata_1_prava_cast;

  DotMatrix #(.inputtype("row"), .matrixcols(32)) dotmatrix_1 ();  // open: row0, row1, row2, row3, row4, row5, row6
  Hex_Digit_Display hex_digit_display_1 (.value(functionality_1_desitky));  // open: dp
  Button button_1 ();  // open: out
  Button button_2 (.out(button_2_out));
  Button button_3 ();  // open: out
  Hex_Digit_Display hex_digit_display_2 (.value(functionality_1_jednotky));  // open: dp
  LED led_1 (.in(\functionality_1_otevírání ));
  LED led_2 (.in(\functionality_1_otevřeno ));
  Button button_4 ();  // open: out
  Button button_5 ();  // open: out
  LED led_3 (.in(\functionality_1_zavřeno ));
  LED led_4 (.in(\functionality_1_zavíraní ));
  functionality functionality_1 (
    .Button(button_2_out), .\Otevírání (\functionality_1_otevírání ),
    .\Otevřeno (\functionality_1_otevřeno ), .\Zavíraní (\functionality_1_zavíraní ),
    .\Zavřeno (\functionality_1_zavřeno ), .Leva(functionality_1_leva), .Prava(functionality_1_prava),
    .Desitky(functionality_1_desitky), .Jednotky(functionality_1_jednotky), .LED(functionality_1_led));
  Button button_6 ();  // open: out
  LED led_5 (.in(functionality_1_led));
  // DotMatrix #(.inputtype("select"), .matrixcols(32), .matrixrows(32)) dotmatrix_2: pin names not known; wires that end beside it: button_2_out, dotmatrix_2_p2, dotmatrix_2_p3
  MatrixVrata matrixvrata_1 (
    .LEVA_CAST(dotmatrix_2_p2), .PRAVA_CAST(matrixvrata_1_prava_cast), .Leve_Dvere(functionality_1_leva),
    .Prave_dvere(functionality_1_prava), .Vyska_dveri(dotmatrix_2_p3));
  // DotMatrix #(.inputtype("select"), .matrixcols(32), .matrixrows(32)) dotmatrix_3: pin names not known; wires that end beside it: matrixvrata_1_prava_cast, dotmatrix_2_p3
  // DotMatrix #(.inputtype("select"), .matrixrows(32)) dotmatrix_4: pin names not known; wires that end beside it: {5{1'b1}}, {32{1'b1}}

  // Notes on the sheet:
  //   PUSTIT AUTO
  //   START/STOP
  //   Tlačítko na projíždějící auto, pustit jen při plně otevřených vratech
  //   Otevírání druhých dveří, když jsou první v polovině
  //   MAYBE: Selectování rychlosti otevírání vrat
  //   Vrátnice
  //   Bug jestli se automaticky dveře zavírají, tak při stisku tlačítka se nezačnou otevírat
endmodule

module buttonswitch (
  input  Reset,
  input  Button,
  output \Output___Otevřeno_Zavřeno 
);

  wire d_ff_1_qn, d_ff_2_q, or_1_out;

  or or_1 (or_1_out, Button, Reset);
  D_Flip_Flop #(.trigger("high")) d_ff_1 (
    .clk(or_1_out), .D(d_ff_2_q), .Q(\Output___Otevřeno_Zavřeno ), .Qn(d_ff_1_qn));  // open: preset, en, reset
  D_Flip_Flop d_ff_2 (.clk(or_1_out), .D(d_ff_1_qn), .Q(d_ff_2_q));  // open: Qn, preset, en, reset
endmodule

module reset (
  input  Leva_Zavirani,
  input  Leva_Zavreno,
  input  Zavrit,
  input  CLOCK,
  output OUTPUT___RESET
);

  wire and_1_out;

  and and_1 (and_1_out, Leva_Zavirani, Leva_Zavreno, Zavrit);
  Counter #(.width(1), .max('h1), .trigger("falling")) counter_1 (
    .count(and_1_out), .carry(OUTPUT___RESET), .clk(CLOCK), .clr(OUTPUT___RESET));  // open: load, D, Q
endmodule

module functionality (
  input  Button,
  output [3:0] Desitky,
  output [3:0] Jednotky,
  output [3:0] Leva,
  output [3:0] Prava,
  output LED,
  output \Otevírání ,
  output \Otevřeno ,
  output \Zavíraní ,
  output \Zavřeno 
);

  wire and_1_out, and_2_out, and_3_out, and_4_out, AR, AUTO_RESET, BR, clock_1_out, comparator_1_gt,
       comparator_2_lt, counter_3_carry, CR, LO, not_1_out, or_1_out, or_2_out, PO, VZ, ZT;
  wire [4:0] counter_3_q;

  Button button_1 ();  // open: out
  Clock #(.highDuration(2), .lowDuration(2)) clock_1 (.out(clock_1_out));
  or or_1 (or_1_out, AUTO_RESET, BR);
  buttonswitch buttonswitch_1 (.Reset(Button), .\Output___Otevřeno_Zavřeno (VZ), .Button(or_1_out));
  display display_1 (
    .\Otevírání (\Otevírání ), .\Pravá_Otevřeno (PO), .\Otevřeno (\Otevřeno ), .\Levá_otevřeno (LO),
    .\Zavřít (ZT), .\Zavírání (\Zavíraní ), .Zapnuto_Vypnuto(VZ), .\Zavřeno (\Zavřeno ), .in_4(Leva));
  and and_1 (and_1_out, ZT, comparator_2_lt);
  and and_2 (and_2_out, VZ, clock_1_out);
  Counter #(.width(4), .max('hf), .ongoal("stay"), .trigger("falling")) counter_1 (
    .load(and_1_out), .Q(Leva), .carry(LO), .clk(and_2_out));  // open: D, count, clr
  zavritdriv zavritdriv_1 (
    .Hodnota_otevreni_zleva(Leva), .On_Off(VZ), .Zavrit_driv(AR), .Button_reset(BR), .Casovac_reset(CR),
    .Auto_Reset(AUTO_RESET));
  Comparator #(.width(4), .mode("unsigned")) comparator_1 (
    .a(Leva), .b(4'b0110), .gt(comparator_1_gt));  // open: eq, lt
  reset reset_1 (
    .Leva_Zavirani(LO), .Leva_Zavreno(and_1_out), .Zavrit(ZT), .OUTPUT___RESET(AUTO_RESET),
    .CLOCK(clock_1_out));
  and and_3 (and_3_out, comparator_1_gt, VZ, clock_1_out);
  Counter #(.width(4), .max('hf), .ongoal("stay"), .trigger("falling")) counter_2 (
    .load(ZT), .Q(Prava), .carry(PO), .clk(and_3_out));  // open: D, count, clr
  Comparator #(.width(4), .mode("unsigned")) comparator_2 (
    .a(Prava), .b(4'b1000), .lt(comparator_2_lt));  // open: gt, eq
  and and_4 (and_4_out, PO, VZ, clock_1_out);
  Counter #(.width(5), .max('h1e), .ongoal("stay")) counter_3 (
    .Q(counter_3_q), .carry(counter_3_carry), .clk(and_4_out), .clr(or_2_out));  // open: load, D, count
  or or_2 (or_2_out, CR, AUTO_RESET);
  or or_3 (ZT, counter_3_carry, AR);
  and and_5 (LED, VZ, clock_1_out);
  not not_1 (not_1_out, AR);
  hexdisplaycasovac hexdisplaycasovac_1 (.in_1(counter_3_q), .desitky(Desitky), .Jednotky(Jednotky), .in_2(not_1_out));

  // Other names for the same wires on the sheet: LH[3:0] = Leva; PH[3:0] = Prava
endmodule

module display (
  input  \Pravá_Otevřeno ,
  input  \Levá_otevřeno ,
  input  \Zavřít ,
  input  [3:0] in_4,
  input  Zapnuto_Vypnuto,
  output \Otevírání ,
  output \Otevřeno ,
  output \Zavírání ,
  output \Zavřeno 
);

  wire and_2_out, and_3_out, and_4_out, and_5_out, not_1_out, not_2_out, not_3_out, not_4_out, not_5_out;

  Comparator #(.width(4), .mode("unsigned")) comparator_1 (.a(in_4), .b(4'b0000), .eq(\Zavřeno ));  // open: gt, lt
  not not_1 (not_1_out, \Zavřít );
  not not_2 (not_2_out, \Pravá_Otevřeno );
  not not_3 (not_3_out, \Zavřít );
  not not_4 (not_4_out, \Pravá_Otevřeno );
  not not_5 (not_5_out, \Levá_otevřeno );
  and and_1 (\Otevírání , Zapnuto_Vypnuto, not_1_out, not_2_out);
  and and_2 (and_2_out, \Pravá_Otevřeno , not_3_out);
  and and_3 (and_3_out, not_4_out, \Zavřít );
  and and_4 (and_4_out, not_5_out, \Zavřít );
  or or_1 (\Zavírání , and_3_out, and_4_out);
  or or_2 (\Otevřeno , and_2_out, and_5_out);
  and and_5 (and_5_out, ~\Otevírání , ~\Zavírání , ~\Zavřeno );  // AND_Gate
endmodule

module zavritdriv (
  input  [3:0] Hodnota_otevreni_zleva,
  input  On_Off,
  input  Auto_Reset,
  output Zavrit_driv,
  output Button_reset,
  output Casovac_reset
);

  wire and_1_out, comparator_1_eq, comparator_1_gt, counter_1_carry, or_1_out;

  or or_1 (or_1_out, and_1_out, Button_reset, Auto_Reset);
  and and_1 (and_1_out, ~On_Off, counter_1_carry);  // AND_Gate
  Comparator #(.width(4), .mode("unsigned")) comparator_1 (
    .a(Hodnota_otevreni_zleva), .b(4'b0000), .gt(comparator_1_gt), .eq(comparator_1_eq));  // open: lt
  Counter #(.width(2), .max('h2), .ongoal("stay")) counter_1 (
    .carry(counter_1_carry), .clk(On_Off), .clr(or_1_out));  // open: load, D, count, Q
  and and_2 (Zavrit_driv, comparator_1_gt, counter_1_carry);
  and and_3 (Button_reset, comparator_1_eq, counter_1_carry);
  or or_2 (Casovac_reset, Button_reset, and_1_out);
endmodule

module MatrixVrata (
  input  [3:0] Leve_Dvere,
  input  [3:0] Prave_dvere,
  output [31:0] Vyska_dveri,
  output [31:0] LEVA_CAST,
  output [31:0] PRAVA_CAST
);

  Multiplexer #(.select(4), .width(32)) multiplexer_1 (
    .in0({32{1'b1}}), .in1(32'hfffffff), .in2(32'h3ffffff), .in3(32'hffffff), .in4(32'h3fffff),
    .in5(32'hfffff), .in6(32'h3ffff), .in7(32'hffff), .in8(32'h3fff), .in9(32'hfff), .in10(32'h3ff),
    .in11(32'hff), .in12(32'h3f), .in13(32'hf), .in14(32'h3), .in15({32{1'b0}}), .out(LEVA_CAST),
    .sel(Leve_Dvere));  // open: en
  Multiplexer #(.select(4), .width(32)) multiplexer_2 (
    .in0({32{1'b1}}), .in1(32'hfffffff0), .in2(32'hffffffc0), .in3(32'hffffff00), .in4(32'hfffffc00),
    .in5(32'hfffff000), .in6(32'hffffc000), .in7(32'hffff0000), .in8(32'hfffc0000), .in9(32'hfff00000),
    .in10(32'hffc00000), .in11(32'hff000000), .in12(32'hfc000000), .in13(32'hf0000000), .in14(32'hc0000000),
    .in15({32{1'b0}}), .out(PRAVA_CAST), .sel(Prave_dvere));  // open: en

  assign Vyska_dveri = 32'hfffffff;
endmodule

module hexdisplaycasovac (
  input  [4:0] in_1,
  input  in_2,
  output [3:0] desitky,
  output [3:0] Jednotky
);

  wire and_1_out, and_2_out, comparator_1_eq, comparator_1_gt, comparator_1_lt, comparator_2_gt,
       comparator_3_gt, or_1_out;
  wire [4:0] controlled_buffer_1_out, subtractor_1_out, subtractor_2_out, subtractor_3_out, subtractor_4_out;
  wire [4:4] controlled_buffer_6_out;

  assign controlled_buffer_1_out = in_2 ? subtractor_1_out : 5'bz;  // Controlled_Buffer controlled_buffer_1
  Subtractor #(.width(5)) subtractor_1 (.a(5'b11110), .b(in_1), .out(subtractor_1_out));  // open: bin, bout
  Comparator #(.width(5), .mode("unsigned")) comparator_1 (
    .a(controlled_buffer_1_out), .b(5'b01001), .gt(comparator_1_gt), .eq(comparator_1_eq),
    .lt(comparator_1_lt));
  Comparator #(.width(5), .mode("unsigned")) comparator_2 (
    .a(controlled_buffer_1_out), .b(5'b10011), .gt(comparator_2_gt));  // open: eq, lt
  Comparator #(.width(5), .mode("unsigned")) comparator_3 (
    .a(controlled_buffer_1_out), .b(5'b11101), .gt(comparator_3_gt));  // open: eq, lt
  Subtractor #(.width(5)) subtractor_2 (
    .a(controlled_buffer_1_out), .b(5'b01010), .out(subtractor_2_out));  // open: bin, bout
  Subtractor #(.width(5)) subtractor_3 (
    .a(controlled_buffer_1_out), .b(5'b10100), .out(subtractor_3_out));  // open: bin, bout
  Subtractor #(.width(5)) subtractor_4 (
    .a(controlled_buffer_1_out), .b(5'b11110), .out(subtractor_4_out));  // open: bin, bout
  or or_1 (or_1_out, comparator_1_lt, comparator_1_eq);
  and and_1 (and_1_out, comparator_1_gt, ~comparator_2_gt);  // AND_Gate
  and and_2 (and_2_out, comparator_2_gt, ~comparator_3_gt);  // AND_Gate
  assign desitky = or_1_out ? 4'b0000 : 4'bz;  // Controlled_Buffer controlled_buffer_2
  assign desitky = and_1_out ? 4'b0001 : 4'bz;  // Controlled_Buffer controlled_buffer_3
  assign desitky = and_2_out ? 4'b0010 : 4'bz;  // Controlled_Buffer controlled_buffer_4
  assign desitky = comparator_3_gt ? 4'b0011 : 4'bz;  // Controlled_Buffer controlled_buffer_5
  assign {controlled_buffer_6_out[4], Jednotky} = or_1_out ? controlled_buffer_1_out : 5'bz;  // Controlled_Buffer controlled_buffer_6
  assign {controlled_buffer_6_out[4], Jednotky} = and_1_out ? subtractor_2_out : 5'bz;  // Controlled_Buffer controlled_buffer_7
  assign {controlled_buffer_6_out[4], Jednotky} = and_2_out ? subtractor_3_out : 5'bz;  // Controlled_Buffer controlled_buffer_8
  assign {controlled_buffer_6_out[4], Jednotky} = comparator_3_gt ? subtractor_4_out : 5'bz;  // Controlled_Buffer controlled_buffer_9
  // also tied to GND on the sheet: controlled_buffer_6_out[4]
endmodule
